# Fritzing sketch drum-booth-controller (saved by Fritzing 0.9.4)

parts:
  Raspberry_Pi_1 = Raspberry Pi 3 [part_number=RPI-3-V1.2]  # not connected
  Onderdeel1 = Arduino Uno (Rev3)
  Part1 = ws2812b [package="smd 2812b"]
  Part2 = ws2812b [package="smd 2812b"]
  Part3 = ws2812b [package="smd 2812b"]

nets:
  N1: Onderdeel1.D8, Part1.DIN
  VSS: Onderdeel1.GND, Part1.VSS, Part2.VSS, Part3.VSS
  N2: Onderdeel1.D6_PWM, Part3.DIN
  N3: Onderdeel1.D7, Part2.DIN
  VDD: Onderdeel1.5V, Part1.VDD, Part2.VDD, Part3.VDD
