# Fritzing sketch wirings (saved by Fritzing 0.9.3b)
breadboards: 1

parts:
  Onderdeel1 = Arduino Nano (Rev3.0) (ICSP)
  Onderdeel3 = NRF24L01+ Breakout Board
  S1 = Toggle Switch [package=THT]
  R1 = Resistor [tolerance=±5% resistance=10k package="0402 [SMD]"]
  Onderdeel2 = ws2812b [package="smd 2812b"]
  U2 = POT [package=pot_alpha_rv16af-20]
  U3 = POT [package=pot_alpha_rv16af-20]
  U4 = POT [package=pot_alpha_rv16af-20]
  C1 = Electrolytic Capacitor [capacitance=1µF package="100 mil [THT, electrolytic]"]

nets:
  GND: Onderdeel1.GND, Onderdeel3.GND, R1.Pin_0, Onderdeel2.VSS, U2.E, U3.E, U4.E
  N1: Onderdeel1.D2, S1.COM
  N2: Onderdeel1.D5, Onderdeel2.DIN
  N3: Onderdeel1.D9, Onderdeel3.CE
  N4: Onderdeel1.D10, Onderdeel3.CS
  N5: Onderdeel1.D11/MOSI, Onderdeel3.MOSI
  N6: Onderdeel1.D12/MISO, Onderdeel3.MISO
  5V: Onderdeel1.5V, S1.L1, Onderdeel2.VDD, U2.A, U3.A, U4.A
  N7: Onderdeel1.A2, U4.S
  N8: Onderdeel1.A1, U3.S
  N9: Onderdeel1.A0, U2.S
  N10: Onderdeel1.3V3, C1.+
  N11: Onderdeel1.D13/SCK, Onderdeel3.SCK
  N12: Onderdeel3.VCC, C1.-
  N13: S1.L2, R1.Pin_1
