# Fritzing sketch wirings (saved by Fritzing 0.9.3b)
breadboards: 1

parts:
  Onderdeel1 = Arduino Nano (Rev3.0) (ICSP)
  RE1 = Hexadecimal Rotary Encoder [part_number=APEM-PT65-303 package=THT]
  Onderdeel2 = ws2812b [package="smd 2812b"]  # not connected
  Onderdeel3 = NRF24L01+ Breakout Board  # not connected

nets:
  N1: Onderdeel1.D2, RE1.Output1Pin
  N2: Onderdeel1.D3, RE1.Output2Pin
  N3: Onderdeel1.D4, RE1.Output4Pin
  N4: Onderdeel1.D5, RE1.Output8pin
  N5: Onderdeel1.5V, RE1.InputCommon, RE1.InputCommon2
